# Fritzing sketch Z-Uno bmp180-oled (saved by Fritzing 0.9.2b)
breadboards: 1

parts:
  Z-uno_2_1 = Z-Uno 2.0
  Часть1 = BMP180 Breakout (GY-68)  # not connected
  Squix1 = OLED 0.96" 128x64 I2C SSD1306

nets:
  N1: Z-uno_2_1.GND#3, Squix1.GND
  N2: Z-uno_2_1.3V3#4, Squix1.VCC
  N3: Z-uno_2_1.pin8, Z-uno_2_1.ANT
  N4: Z-uno_2_1.ANT_U.FL, Z-uno_2_1.pin9, Squix1.SCL
  N5: Z-uno_2_1.pin10, Squix1.SCA
  N6: Z-uno_2_1.pin_22, Z-uno_2_1.3V3#44
  N7: Z-uno_2_1.pin_23, Z-uno_2_1.GND#43

custom parts:
  Z-Uno 2.0: The Teensy is a complete USB-based microcontoller development system, in a very small footprint, capable of implementing many types of projects. All programming is done via the USB port. No special programmer is needed, only a standard micro-USB cable and a PC or Macintosh with a USB port. It has a USB keyboard/mouse/joystick emulation stack and can be programmed through Arduino IDE. Z-Uno is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
  BMP180 Breakout (GY-68): This is a simple breakout board for the BMP180, a high-precision, low-power barometric pressure sensor made by Bosch Sensortec. The range of measurement is from 300hPa to 1100hPa. The sensor can be supplied with voltage ranging from 1.8V to 3.6V. Operating temperature range is -40 to +85 °C. This particular breakout board (or perhaps the configuration) is produced by Shenzhen Keep Power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
